// Logisim project Y86.circ as structural Verilog: 7 circuits, main circuit Datapath
// imemError
module Datapath (
  input  ClearData,
  input  Reset
);

  wire and_1_out, Clock_out, dmemError, imemError, not_1_out, Y86_Control_alubsrc, Y86_Control_aluop,
       Y86_Control_continue, Y86_Control_dmemaddr, Y86_Control_dmemdata, Y86_Control_dmemwrite,
       Y86_Control_dstmsrc, Y86_Control_setcc, Y86_Control_statwrite, Y86_Control_valasrc,
       Y86_Control_valbsrc, Y86_Control_valcsrc;
  wire [1:0] Stat_q, Y86_Control_aluasrc, Y86_Control_dstesrc, Y86_Control_newpc, Y86_Control_pcincsrc,
       Y86_Control_statval;
  wire [2:0] alu_1_of, CC_q;
  wire [3:0] ISplit_icode, ISplit_ifun, ISplit_ra, ISplit_rb, multiplexer_2_out, multiplexer_3_out,
       multiplexer_4_out, multiplexer_5_out, multiplexer_9_out;
  wire [7:0] IMem_b0, IMem_b1, IMem_b2, IMem_b3, IMem_b4, IMem_b5;
  wire [9:0] DAddr_2_wordaddr;
  wire [31:0] adder_1_out, alu_1_vale, ISplit_d_v, ISplit_dest, multiplexer_1_out, multiplexer_6_out,
       multiplexer_7_out, multiplexer_8_out, multiplexer_10_out, multiplexer_11_out, multiplexer_12_out,
       PC_q, PChold_q, ram_1_data, Registers_vala, Registers_valb;

  and and_1 (and_1_out, Clock_out, Y86_Control_continue);
  Clock Clock (.out(Clock_out));
  Multiplexer #(.select(2), .width(32), .enable("false")) multiplexer_1 (
    .in0(32'h1), .in1(32'h2), .in2(32'h5), .in3(32'h6), .out(multiplexer_1_out), .sel(Y86_Control_pcincsrc));
  Register #(.width(32)) PC (.D(PChold_q), .Q(PC_q), .clk(and_1_out), .clr(Reset));  // open: en
  not not_1 (not_1_out, and_1_out);
  Register #(.width(2)) Stat (
    .D(Y86_Control_statval), .en(Y86_Control_statwrite), .Q(Stat_q), .clk(not_1_out), .clr(Reset));
  Adder #(.width(32)) adder_1 (.a(multiplexer_1_out), .b(PC_q), .out(adder_1_out));  // open: cin, cout
  Memory IMem (
    .ReadAddr(PC_q), .imemError(imemError), .B0(IMem_b0), .B1(IMem_b1), .B2(IMem_b2), .B3(IMem_b3),
    .B4(IMem_b4), .B5(IMem_b5));
  // Probe on adder_1_out
  // Probe on ISplit_ra
  // Probe on ISplit_rb
  InstrSplit ISplit (
    .B0(IMem_b0), .B1(IMem_b1), .B2(IMem_b2), .B3(IMem_b3), .B4(IMem_b4), .B5(IMem_b5), .icode(ISplit_icode),
    .ifun(ISplit_ifun), .rA(ISplit_ra), .rB(ISplit_rb), .Dest(ISplit_dest), .D_V(ISplit_d_v));
  Multiplexer #(.width(4), .enable("false")) multiplexer_2 (
    .in0(ISplit_ra), .in1(4'b0100), .out(multiplexer_2_out), .sel(Y86_Control_valasrc));
  Multiplexer #(.width(4), .enable("false")) multiplexer_3 (
    .in0(ISplit_rb), .in1(4'b0100), .out(multiplexer_3_out), .sel(Y86_Control_valbsrc));
  Multiplexer #(.select(2), .width(4), .enable("false")) multiplexer_4 (
    .in0(ISplit_rb), .in1(4'b0100), .in2(4'b1111), .in3(4'b1111), .out(multiplexer_4_out),
    .sel(Y86_Control_dstesrc));
  Multiplexer #(.width(4), .enable("false")) multiplexer_5 (
    .in0(ISplit_ra), .in1(4'b1111), .out(multiplexer_5_out), .sel(Y86_Control_dstmsrc));
  Multiplexer #(.width(32), .enable("false")) multiplexer_6 (
    .in0(ISplit_dest), .in1(ISplit_d_v), .out(multiplexer_6_out), .sel(Y86_Control_valcsrc));
  Y86Control Y86_Control (
    .icode(ISplit_icode), .ifun(ISplit_ifun), .CC(CC_q), .Stat(Stat_q), .imemError(imemError),
    .dmemError(dmemError), .\continue (Y86_Control_continue), .statWrite(Y86_Control_statwrite),
    .statVal(Y86_Control_statval), .PCIncSrc(Y86_Control_pcincsrc), .valCsrc(Y86_Control_valcsrc),
    .valAsrc(Y86_Control_valasrc), .valBsrc(Y86_Control_valbsrc), .dstMsrc(Y86_Control_dstmsrc),
    .aluAsrc(Y86_Control_aluasrc), .aluBsrc(Y86_Control_alubsrc), .setCC(Y86_Control_setcc),
    .aluOp(Y86_Control_aluop), .dmemAddr(Y86_Control_dmemaddr), .dmemData(Y86_Control_dmemdata),
    .dmemWrite(Y86_Control_dmemwrite), .newPC(Y86_Control_newpc), .dstEsrc(Y86_Control_dstesrc));
  // Probe on multiplexer_6_out
  // Probe on Registers_vala
  // Probe on Registers_valb
  RegisterFile Registers (
    .srcA(multiplexer_2_out), .srcB(multiplexer_3_out), .dstE(multiplexer_4_out), .valE(alu_1_vale),
    .dstM(multiplexer_5_out), .valM(ram_1_data), .Clock(not_1_out), .Clear(Reset), .valA(Registers_vala),
    .valB(Registers_valb));
  Multiplexer #(.select(2), .width(32), .enable("false")) multiplexer_7 (
    .in0(Registers_vala), .in1(multiplexer_6_out), .in2(32'h4), .in3(32'hfffffffc), .out(multiplexer_7_out),
    .sel(Y86_Control_aluasrc));
  Multiplexer #(.width(32), .enable("false")) multiplexer_8 (
    .in0(Registers_valb), .in1({32{1'b0}}), .out(multiplexer_8_out), .sel(Y86_Control_alubsrc));
  ALU alu_1 (
    .ALU_A(multiplexer_7_out), .ALU_B(multiplexer_8_out), .ZF(alu_1_of[2]), .SF(alu_1_of[1]),
    .OF(alu_1_of[0]), .ALUfun(multiplexer_9_out), .valE(alu_1_vale));
  Multiplexer #(.width(4), .enable("false")) multiplexer_9 (
    .in0(4'b0000), .in1(ISplit_ifun), .out(multiplexer_9_out), .sel(Y86_Control_aluop));
  // Probe on alu_1_vale
  Register #(.width(3)) CC (.D(alu_1_of), .en(Y86_Control_setcc), .Q(CC_q), .clk(not_1_out), .clr(Reset));
  // Probe on multiplexer_10_out
  DMemAddr DAddr_2 (.AddrIn(multiplexer_10_out), .dmemerr(dmemError), .WordAddr(DAddr_2_wordaddr));
  Multiplexer #(.width(32), .enable("false")) multiplexer_10 (
    .in0(alu_1_vale), .in1(Registers_vala), .out(multiplexer_10_out), .sel(Y86_Control_dmemaddr));
  Multiplexer #(.width(32), .enable("false")) multiplexer_11 (
    .in0(Registers_vala), .in1(adder_1_out), .out(multiplexer_11_out), .sel(Y86_Control_dmemdata));
  // Probe on ram_1_data
  RAM #(.addrWidth(10), .dataWidth(32), .bus("separate")) ram_1 (
    .addr(DAddr_2_wordaddr), .din(multiplexer_11_out), .data(ram_1_data), .str(Y86_Control_dmemwrite),
    .clk(not_1_out), .ld(1'b1), .clr(ClearData));  // open: sel
  // Probe on multiplexer_12_out
  Multiplexer #(.select(2), .width(32), .enable("false")) multiplexer_12 (
    .in0(adder_1_out), .in1(multiplexer_6_out), .in2(ram_1_data), .out(multiplexer_12_out),
    .sel(Y86_Control_newpc));  // open: in3
  Register #(.width(32)) PChold (.D(multiplexer_12_out), .Q(PChold_q), .clk(not_1_out));  // open: en, clr

  // Notes on the sheet:
  //   valP
  //   valC
  //   valA
  //   valB
  //   valE
  //   ALU
  //   valM
endmodule

module InstrSplit (
  input  [7:0] B0,
  input  [7:0] B1,
  input  [7:0] B2,
  input  [7:0] B3,
  input  [7:0] B4,
  input  [7:0] B5,
  output [3:0] icode,
  output [3:0] ifun,
  output [3:0] rA,
  output [3:0] rB,
  output [31:0] Dest,
  output [31:0] D_V
);


  assign D_V = {B5, B4, B3, B2};
  assign Dest = {B4, B3, B2, B1};
  assign icode = B0[7:4];
  assign ifun = B0[3:0];
  assign rA = B1[7:4];
  assign rB = B1[3:0];
endmodule

module RegisterFile (
  input  [3:0] srcA,
  input  [3:0] srcB,
  input  [3:0] dstE,
  input  [31:0] valE,
  input  [3:0] dstM,
  input  [31:0] valM,
  input  Clock,
  input  Clear,
  output [31:0] valA,
  output [31:0] valB
);

  wire demultiplexer_1_out0, demultiplexer_1_out1, demultiplexer_1_out2, demultiplexer_1_out3,
       demultiplexer_1_out4, demultiplexer_1_out5, demultiplexer_1_out6, demultiplexer_1_out7,
       demultiplexer_2_out0, demultiplexer_2_out1, demultiplexer_2_out2, demultiplexer_2_out3,
       demultiplexer_2_out4, demultiplexer_2_out5, demultiplexer_2_out6, demultiplexer_2_out7, not_1_out,
       not_2_out, regwrite_1_enable, regwrite_2_enable, regwrite_3_enable, regwrite_4_enable,
       regwrite_5_enable, regwrite_6_enable, regwrite_7_enable, regwrite_8_enable;
  wire [31:0] register_1_q, register_2_q, register_3_q, register_4_q, register_5_q, register_6_q,
       register_7_q, register_8_q, regwrite_1_data, regwrite_2_data, regwrite_3_data, regwrite_4_data,
       regwrite_5_data, regwrite_6_data, regwrite_7_data, regwrite_8_data;

  not not_1 (not_1_out, dstE[3]);
  not not_2 (not_2_out, dstM[3]);
  Demultiplexer #(.select(3), .enable("false")) demultiplexer_1 (
    .out0(demultiplexer_1_out0), .out1(demultiplexer_1_out1), .out2(demultiplexer_1_out2),
    .out3(demultiplexer_1_out3), .out4(demultiplexer_1_out4), .out5(demultiplexer_1_out5),
    .out6(demultiplexer_1_out6), .out7(demultiplexer_1_out7), .in(not_1_out), .sel(dstE[2:0]));
  Demultiplexer #(.select(3), .enable("false")) demultiplexer_2 (
    .out0(demultiplexer_2_out0), .out1(demultiplexer_2_out1), .out2(demultiplexer_2_out2),
    .out3(demultiplexer_2_out3), .out4(demultiplexer_2_out4), .out5(demultiplexer_2_out5),
    .out6(demultiplexer_2_out6), .out7(demultiplexer_2_out7), .in(not_2_out), .sel(dstM[2:0]));
  Register #(.width(32)) register_1 (
    .D(regwrite_1_data), .en(regwrite_1_enable), .Q(register_1_q), .clk(Clock), .clr(Clear));
  RegWrite regwrite_1 (
    .dstE(demultiplexer_1_out0), .dstM(demultiplexer_2_out0), .valE(valE), .valM(valM),
    .Data(regwrite_1_data), .Enable(regwrite_1_enable));
  RegWrite regwrite_2 (
    .dstE(demultiplexer_1_out1), .dstM(demultiplexer_2_out1), .valE(valE), .valM(valM),
    .Data(regwrite_2_data), .Enable(regwrite_2_enable));
  Register #(.width(32)) register_2 (
    .D(regwrite_2_data), .en(regwrite_2_enable), .Q(register_2_q), .clk(Clock), .clr(Clear));
  RegWrite regwrite_3 (
    .dstE(demultiplexer_1_out2), .dstM(demultiplexer_2_out2), .valE(valE), .valM(valM),
    .Data(regwrite_3_data), .Enable(regwrite_3_enable));
  Register #(.width(32)) register_3 (
    .D(regwrite_3_data), .en(regwrite_3_enable), .Q(register_3_q), .clk(Clock), .clr(Clear));
  Register #(.width(32)) register_4 (
    .D(regwrite_4_data), .en(regwrite_4_enable), .Q(register_4_q), .clk(Clock), .clr(Clear));
  RegWrite regwrite_4 (
    .dstE(demultiplexer_1_out3), .dstM(demultiplexer_2_out3), .valE(valE), .valM(valM),
    .Data(regwrite_4_data), .Enable(regwrite_4_enable));
  RegWrite regwrite_5 (
    .dstE(demultiplexer_1_out4), .dstM(demultiplexer_2_out4), .valE(valE), .valM(valM),
    .Data(regwrite_5_data), .Enable(regwrite_5_enable));
  Register #(.width(32)) register_5 (
    .D(regwrite_5_data), .en(regwrite_5_enable), .Q(register_5_q), .clk(Clock), .clr(Clear));
  RegWrite regwrite_6 (
    .dstE(demultiplexer_1_out5), .dstM(demultiplexer_2_out5), .valE(valE), .valM(valM),
    .Data(regwrite_6_data), .Enable(regwrite_6_enable));
  Register #(.width(32)) register_6 (
    .D(regwrite_6_data), .en(regwrite_6_enable), .Q(register_6_q), .clk(Clock), .clr(Clear));
  Register #(.width(32)) register_7 (
    .D(regwrite_7_data), .en(regwrite_7_enable), .Q(register_7_q), .clk(Clock), .clr(Clear));
  RegWrite regwrite_7 (
    .dstE(demultiplexer_1_out6), .dstM(demultiplexer_2_out6), .valE(valE), .valM(valM),
    .Data(regwrite_7_data), .Enable(regwrite_7_enable));
  RegWrite regwrite_8 (
    .dstE(demultiplexer_1_out7), .dstM(demultiplexer_2_out7), .valE(valE), .valM(valM),
    .Data(regwrite_8_data), .Enable(regwrite_8_enable));
  Register #(.width(32)) register_8 (
    .D(regwrite_8_data), .en(regwrite_8_enable), .Q(register_8_q), .clk(Clock), .clr(Clear));
  Multiplexer #(.select(3), .width(32), .enable("false")) multiplexer_1 (
    .in0(register_1_q), .in1(register_2_q), .in2(register_3_q), .in3(register_4_q), .in4(register_5_q),
    .in5(register_6_q), .in6(register_7_q), .in7(register_8_q), .out(valA), .sel(srcA[2:0]));
  Multiplexer #(.select(3), .width(32), .enable("false")) multiplexer_2 (
    .in0(register_1_q), .in1(register_2_q), .in2(register_3_q), .in3(register_4_q), .in4(register_5_q),
    .in5(register_6_q), .in6(register_7_q), .in7(register_8_q), .out(valB), .sel(srcB[2:0]));
endmodule

module ALU (
  input  [31:0] ALU_A,
  input  [31:0] ALU_B,
  input  [3:0] ALUfun,
  output ZF,
  output SF,
  output OF,
  output [31:0] valE
);

  wire msb_1_msb, msb_2_msb, msb_3_msb, or_1_out, xnor_1_out, xor_1_out;
  wire [5:0] bitadder_1_out;
  wire [31:0] adder_1_out, and_2_out, multiplexer_1_out, multiplexer_2_out, not_1_out, xor_2_out;

  assign not_1_out = ~ALU_A;  // NOT_Gate not_1, 32 bits wide
  xnor xnor_1 (xnor_1_out, msb_2_msb, msb_1_msb);
  MSB msb_1 (.MSB(msb_1_msb), .Value(ALU_B));
  MSB msb_2 (.MSB(msb_2_msb), .Value(multiplexer_1_out));
  Multiplexer #(.width(32), .enable("false")) multiplexer_1 (
    .in0(ALU_A), .in1(not_1_out), .out(multiplexer_1_out), .sel(ALUfun[0]));
  and and_1 (OF, xnor_1_out, xor_1_out);
  Adder #(.width(32)) adder_1 (.a(ALU_B), .b(multiplexer_1_out), .out(adder_1_out), .cin(ALUfun[0]));  // open: cout
  xor xor_1 (xor_1_out, msb_1_msb, msb_3_msb);
  MSB msb_3 (.MSB(msb_3_msb), .Value(adder_1_out));
  assign and_2_out = ALU_A & ALU_B;  // AND_Gate and_2, 32 bits wide
  assign xor_2_out = ALU_A ^ ALU_B;  // XOR_Gate xor_2, 32 bits wide
  Multiplexer #(.width(32), .enable("false")) multiplexer_2 (
    .in0(and_2_out), .in1(xor_2_out), .out(multiplexer_2_out), .sel(ALUfun[0]));
  MSB msb_4 (.MSB(SF), .Value(valE));
  not not_2 (ZF, or_1_out);
  Multiplexer #(.width(32), .enable("false")) multiplexer_3 (
    .in0(adder_1_out), .in1(multiplexer_2_out), .out(valE), .sel(ALUfun[1]));
  or or_1 (or_1_out, bitadder_1_out[5], bitadder_1_out[4], bitadder_1_out[3], bitadder_1_out[2], bitadder_1_out[1], bitadder_1_out[0]);
  BitAdder #(.width(32)) bitadder_1 (.in0(valE), .out(bitadder_1_out));
endmodule

module DMemAddr (
  input  [31:0] AddrIn,
  output dmemerr,
  output [9:0] WordAddr
);

  wire or_2_out;

  or or_1 (dmemerr, AddrIn[0], AddrIn[1], or_2_out);
  or or_2 (or_2_out, AddrIn[12], AddrIn[13], AddrIn[14], AddrIn[15], AddrIn[16], AddrIn[17], AddrIn[18], AddrIn[19], AddrIn[20], AddrIn[21], AddrIn[22], AddrIn[23], AddrIn[24], AddrIn[25], AddrIn[26], AddrIn[27], AddrIn[28], AddrIn[29], AddrIn[30], AddrIn[31]);

  assign WordAddr = AddrIn[11:2];
endmodule

module MSB (
  input  [31:0] Value,
  output MSB
);


  assign MSB = Value[31];
endmodule

module RegWrite (
  input  dstE,
  input  dstM,
  input  [31:0] valE,
  input  [31:0] valM,
  output [31:0] Data,
  output Enable
);

  or or_1 (Enable, dstE, dstM);
  Multiplexer #(.width(32), .enable("false")) multiplexer_1 (.in0(valE), .in1(valM), .out(Data), .sel(dstM));
endmodule
