// Logisim project Y86Control.circ as structural Verilog: 17 circuits, main circuit Y86Control
module Y86Control (
  input  [3:0] icode,
  input  [3:0] ifun,
  input  [2:0] CC,
  input  [1:0] Stat,
  input  imemError,
  input  dmemError,
  output \continue ,
  output statWrite,
  output [1:0] statVal,
  output [1:0] PCIncSrc,
  output valCsrc,
  output valAsrc,
  output valBsrc,
  output [1:0] dstEsrc,
  output dstMsrc,
  output [1:0] aluAsrc,
  output aluBsrc,
  output setCC,
  output aluOp,
  output dmemAddr,
  output dmemData,
  output dmemWrite,
  output [1:0] newPC
);

  nor nor_1 (\continue , Stat[1], Stat[0]);
  newstatVal newstatval_1 (
    .statWrite(statWrite), .ifun(ifun), .dmem(dmemError), .imem(imemError), .icode(icode), .statVal(statVal));
  PCIncSrc pcincsrc_1 (.PCIncSrc(PCIncSrc), .Icode(icode));
  valCsrc valcsrc_1 (.valC(valCsrc), .icode(icode));
  valAsrc valasrc_1 (.valA(valAsrc), .icode(icode));
  valBsrc valbsrc_1 (.valB(valBsrc), .icode(icode));
  dstEsrc dstesrc_1 (.dstEsrc(dstEsrc), .CC(CC), .ifun(ifun), .icode(icode));
  dstMsrc dstmsrc_1 (.dstMsrc(dstMsrc), .icode(icode));
  aluAsrc aluasrc_1 (.aluAsrc(aluAsrc), .icode(icode));
  setCC setcc_1 (.setCC(setCC), .icode(icode));
  aluBsrc alubsrc_1 (.dstMsrc(aluBsrc), .icode(icode));
  aluOp aluop_1 (.aluOp(aluOp), .icode(icode));
  dmemAddr dmemaddr_1 (.dmemAddr(dmemAddr), .icode(icode));
  dmemData dmemdata_1 (.dmemData(dmemData), .icode(icode));
  dmemWrite dmemwrite_1 (.dmemWrite(dmemWrite), .icode(icode));
  NewPC newpc_1 (.newPC(newPC), .CC(CC), .ifun(ifun), .icode(icode));
endmodule

// PCInc
module PCIncSrc (
  input  [3:0] Icode,
  output [1:0] PCIncSrc
);

  Multiplexer #(.select(4), .width(2)) multiplexer_1 (
    .in0(2'b00), .in1(2'b00), .in2(2'b01), .in3(2'b11), .in4(2'b11), .in5(2'b11), .in6(2'b01), .in7(2'b10),
    .in8(2'b10), .in9(2'b00), .in10(2'b01), .in11(2'b01), .in12(2'b00), .in13(2'b00), .in14(2'b00),
    .in15(2'b00), .out(PCIncSrc), .sel(Icode));  // open: en
endmodule

// newPC
module NewPC (
  input  [3:0] ifun,
  input  [3:0] icode,
  input  [2:0] CC,
  output [1:0] newPC
);

  wire and_1_out, not_1_out, not_2_out, not_3_out, not_4_out, or_1_out, xor_1_out, xor_2_out, xor_3_out,
       xor_4_out;
  wire [1:0] multiplexer_1_out, multiplexer_2_out, multiplexer_3_out, multiplexer_4_out, multiplexer_5_out,
       multiplexer_6_out, multiplexer_7_out;

  xor xor_1 (xor_1_out, CC[1], CC[0]);
  not not_1 (not_1_out, CC[2]);
  not not_2 (not_2_out, CC[2]);
  and and_1 (and_1_out, not_2_out, not_3_out);
  not not_3 (not_3_out, xor_1_out);
  xor xor_2 (xor_2_out, CC[1], CC[0]);
  not not_4 (not_4_out, xor_2_out);
  xor xor_3 (xor_3_out, CC[1], CC[0]);
  or or_1 (or_1_out, CC[2], xor_4_out);
  xor xor_4 (xor_4_out, CC[1], CC[0]);
  Multiplexer #(.width(2)) multiplexer_1 (
    .in0(2'b00), .in1(2'b01), .out(multiplexer_1_out), .sel(and_1_out));  // open: en
  Multiplexer #(.width(2)) multiplexer_2 (
    .in0(2'b00), .in1(2'b01), .out(multiplexer_2_out), .sel(not_4_out));  // open: en
  Multiplexer #(.width(2)) multiplexer_3 (
    .in0(2'b00), .in1(2'b01), .out(multiplexer_3_out), .sel(not_1_out));  // open: en
  Multiplexer #(.width(2)) multiplexer_4 (.in0(2'b00), .in1(2'b01), .out(multiplexer_4_out), .sel(CC[2]));  // open: en
  Multiplexer #(.width(2)) multiplexer_5 (
    .in0(2'b00), .in1(2'b01), .out(multiplexer_5_out), .sel(xor_3_out));  // open: en
  Multiplexer #(.width(2)) multiplexer_6 (
    .in0(2'b00), .in1(2'b01), .out(multiplexer_6_out), .sel(or_1_out));  // open: en
  Multiplexer #(.select(4), .width(2)) multiplexer_7 (
    .in0(2'b01), .in1(multiplexer_6_out), .in2(multiplexer_5_out), .in3(multiplexer_4_out),
    .in4(multiplexer_3_out), .in5(multiplexer_2_out), .in6(multiplexer_1_out), .in7(2'b11), .in8(2'b11),
    .in9(2'b11), .in10(2'b11), .in11(2'b11), .in12(2'b11), .in13(2'b11), .in14(2'b11), .in15(2'b11),
    .out(multiplexer_7_out), .sel(ifun));  // open: en
  Multiplexer #(.select(4), .width(2)) multiplexer_8 (
    .in0(2'b11), .in1(2'b00), .in2(2'b00), .in3(2'b00), .in4(2'b00), .in5(2'b00), .in6(2'b00),
    .in7(multiplexer_7_out), .in8(2'b01), .in9(2'b10), .in10(2'b00), .in11(2'b00), .in12(2'b00),
    .in13(2'b00), .in14(2'b00), .in15(2'b00), .out(newPC), .sel(icode));  // open: en
endmodule

// statV
module statVal (
  input  [3:0] ifun,
  input  [3:0] icode,
  input  imemError,
  input  dmemError,
  output [1:0] statVal,
  output statWrite
);

  wire and_1_out, multiplexer_1_out, multiplexer_2_out, not_1_out, or_1_out, or_2_out, or_3_out, or_6_out;

  Multiplexer #(.select(4)) multiplexer_1 (
    .in0(1'b0), .in1(1'b0), .in2(1'b0), .in3(1'b0), .in4(1'b0), .in5(1'b0), .in6(1'b0), .in7(1'b1),
    .in8(1'b1), .in9(1'b1), .in10(1'b1), .in11(1'b1), .in12(1'b1), .in13(1'b1), .in14(1'b1), .in15(1'b1),
    .out(multiplexer_1_out), .sel(ifun));  // open: en
  or or_1 (or_1_out, ifun[3], ifun[2]);
  or or_2 (or_2_out, ifun[1], ifun[0], ifun[2], ifun[3]);
  or or_3 (or_3_out, multiplexer_1_out, multiplexer_2_out);
  Multiplexer #(.select(4)) multiplexer_2 (
    .in0(or_2_out), .in1(or_2_out), .in2(multiplexer_1_out), .in3(or_2_out), .in4(or_2_out), .in5(or_2_out),
    .in6(or_1_out), .in7(multiplexer_1_out), .in8(or_2_out), .in9(or_2_out), .in10(or_2_out),
    .in11(or_2_out), .in12(1'b1), .in13(1'b1), .in14(1'b1), .in15(1'b1), .out(multiplexer_2_out), .sel(icode));  // open: en
  or or_4 (statVal[0], or_3_out, dmemError);
  or or_5 (statVal[1], dmemError, imemError);
  not not_1 (not_1_out, dmemError);
  or or_6 (or_6_out, imemError, and_1_out, or_3_out);
  and and_1 (and_1_out, not_1_out, 1'b1);
  Multiplexer #(.select(4)) multiplexer_3 (
    .in0(or_6_out), .in1(or_6_out), .in2(or_6_out), .in3(or_6_out), .in4(1'b1), .in5(1'b1), .in6(or_6_out),
    .in7(or_6_out), .in8(1'b1), .in9(1'b1), .in10(1'b1), .in11(1'b1), .in12(or_6_out), .in13(or_6_out),
    .in14(or_6_out), .in15(or_6_out), .out(statWrite), .sel(icode));  // open: en
endmodule

// valA
module valAsrc (
  input  [3:0] icode,
  output valA
);

  Multiplexer #(.select(4)) multiplexer_1 (
    .in0(1'b0), .in1(1'b0), .in2(1'b0), .in3(1'b0), .in4(1'b0), .in5(1'b0), .in6(1'b0), .in7(1'b0),
    .in8(1'b0), .in9(1'b1), .in10(1'b0), .in11(1'b1), .in12(1'b0), .in13(1'b0), .in14(1'b0), .in15(1'b0),
    .out(valA), .sel(icode));  // open: en
endmodule

// valC
module valCsrc (
  input  [3:0] icode,
  output valC
);

  Multiplexer #(.select(4)) multiplexer_1 (
    .in0(1'b0), .in1(1'b0), .in2(1'b0), .in3(1'b1), .in4(1'b1), .in5(1'b1), .in6(1'b0), .in7(1'b0),
    .in8(1'b0), .in9(1'b0), .in10(1'b0), .in11(1'b0), .in12(1'b0), .in13(1'b0), .in14(1'b0), .in15(1'b0),
    .out(valC), .sel(icode));  // open: en
endmodule

// valB
module valBsrc (
  input  [3:0] icode,
  output valB
);

  Multiplexer #(.select(4)) multiplexer_1 (
    .in0(1'b0), .in1(1'b0), .in2(1'b0), .in3(1'b0), .in4(1'b0), .in5(1'b0), .in6(1'b0), .in7(1'b0),
    .in8(1'b1), .in9(1'b1), .in10(1'b1), .in11(1'b1), .in12(1'b0), .in13(1'b0), .in14(1'b0), .in15(1'b0),
    .out(valB), .sel(icode));  // open: en
endmodule

// dstE
module dstEsrc (
  input  [3:0] ifun,
  input  [3:0] icode,
  input  [2:0] CC,
  output [1:0] dstEsrc
);

  wire and_1_out, not_1_out, not_2_out, not_3_out, not_4_out, or_1_out, xor_1_out, xor_2_out, xor_3_out,
       xor_4_out;
  wire [1:0] multiplexer_1_out, multiplexer_2_out, multiplexer_3_out, multiplexer_4_out, multiplexer_5_out,
       multiplexer_6_out, multiplexer_7_out;

  xor xor_1 (xor_1_out, CC[1], CC[0]);
  not not_1 (not_1_out, CC[2]);
  not not_2 (not_2_out, xor_1_out);
  xor xor_2 (xor_2_out, CC[1], CC[0]);
  not not_3 (not_3_out, CC[2]);
  xor xor_3 (xor_3_out, CC[1], CC[0]);
  xor xor_4 (xor_4_out, CC[1], CC[0]);
  and and_1 (and_1_out, not_1_out, not_2_out);
  not not_4 (not_4_out, xor_2_out);
  or or_1 (or_1_out, CC[2], xor_4_out);
  Multiplexer #(.width(2)) multiplexer_1 (
    .in0(2'b10), .in1(2'b00), .out(multiplexer_1_out), .sel(and_1_out));  // open: en
  Multiplexer #(.width(2)) multiplexer_2 (
    .in0(2'b10), .in1(2'b00), .out(multiplexer_2_out), .sel(not_4_out));  // open: en
  Multiplexer #(.width(2)) multiplexer_3 (
    .in0(2'b10), .in1(2'b00), .out(multiplexer_3_out), .sel(not_3_out));  // open: en
  Multiplexer #(.width(2)) multiplexer_4 (.in0(2'b10), .in1(2'b00), .out(multiplexer_4_out), .sel(CC[2]));  // open: en
  Multiplexer #(.width(2)) multiplexer_5 (
    .in0(2'b10), .in1(2'b00), .out(multiplexer_5_out), .sel(xor_3_out));  // open: en
  Multiplexer #(.width(2)) multiplexer_6 (
    .in0(2'b10), .in1(2'b00), .out(multiplexer_6_out), .sel(or_1_out));  // open: en
  Multiplexer #(.select(4), .width(2)) multiplexer_7 (
    .in0(2'b00), .in1(multiplexer_6_out), .in2(multiplexer_5_out), .in3(multiplexer_4_out),
    .in4(multiplexer_3_out), .in5(multiplexer_2_out), .in6(multiplexer_1_out), .in7(2'b10), .in8(2'b10),
    .in9(2'b10), .in10(2'b10), .in11(2'b10), .in12(2'b10), .in13(2'b10), .in14(2'b10), .in15(2'b10),
    .out(multiplexer_7_out), .sel(ifun));  // open: en
  Multiplexer #(.select(4), .width(2)) multiplexer_8 (
    .in0(2'b10), .in1(2'b10), .in2(multiplexer_7_out), .in3(2'b00), .in4(2'b10), .in5(2'b10), .in6(2'b00),
    .in7(2'b10), .in8(2'b01), .in9(2'b01), .in10(2'b01), .in11(2'b01), .in12(2'b10), .in13(2'b10),
    .in14(2'b10), .in15(2'b10), .out(dstEsrc), .sel(icode));  // open: en
endmodule

// dstM
module dstMsrc (
  input  [3:0] icode,
  output dstMsrc
);

  Multiplexer #(.select(4)) multiplexer_1 (
    .in0(1'b1), .in1(1'b1), .in2(1'b1), .in3(1'b1), .in4(1'b1), .in5(1'b0), .in6(1'b1), .in7(1'b1),
    .in8(1'b1), .in9(1'b1), .in10(1'b1), .in11(1'b0), .in12(1'b0), .in13(1'b0), .in14(1'b0), .in15(1'b0),
    .out(dstMsrc), .sel(icode));  // open: en
endmodule

// aluA
module aluAsrc (
  input  [3:0] icode,
  output [1:0] aluAsrc
);

  Multiplexer #(.select(4), .width(2)) multiplexer_1 (
    .in0(2'b00), .in1(2'b00), .in2(2'b00), .in3(2'b01), .in4(2'b01), .in5(2'b01), .in6(2'b00), .in7(2'b00),
    .in8(2'b11), .in9(2'b10), .in10(2'b11), .in11(2'b10), .in12(2'b00), .in13(2'b00), .in14(2'b00),
    .in15(2'b00), .out(aluAsrc), .sel(icode));  // open: en
endmodule

// aluB
module aluBsrc (
  input  [3:0] icode,
  output dstMsrc
);

  Multiplexer #(.select(4)) multiplexer_1 (
    .in0(1'b0), .in1(1'b0), .in2(1'b1), .in3(1'b1), .in4(1'b0), .in5(1'b0), .in6(1'b0), .in7(1'b0),
    .in8(1'b0), .in9(1'b0), .in10(1'b0), .in11(1'b0), .in12(1'b0), .in13(1'b0), .in14(1'b0), .in15(1'b0),
    .out(dstMsrc), .sel(icode));  // open: en
endmodule

module setCC (
  input  [3:0] icode,
  output setCC
);

  Multiplexer #(.select(4)) multiplexer_1 (
    .in0(1'b0), .in1(1'b0), .in2(1'b0), .in3(1'b0), .in4(1'b0), .in5(1'b0), .in6(1'b1), .in7(1'b0),
    .in8(1'b0), .in9(1'b0), .in10(1'b0), .in11(1'b0), .in12(1'b0), .in13(1'b0), .in14(1'b0), .in15(1'b0),
    .out(setCC), .sel(icode));  // open: en
endmodule

module aluOp (
  input  [3:0] icode,
  output aluOp
);

  Multiplexer #(.select(4)) multiplexer_1 (
    .in0(1'b0), .in1(1'b0), .in2(1'b0), .in3(1'b0), .in4(1'b0), .in5(1'b0), .in6(1'b1), .in7(1'b0),
    .in8(1'b0), .in9(1'b0), .in10(1'b0), .in11(1'b0), .in12(1'b0), .in13(1'b0), .in14(1'b0), .in15(1'b0),
    .out(aluOp), .sel(icode));  // open: en
endmodule

// adr
module dmemAddr (
  input  [3:0] icode,
  output dmemAddr
);

  Multiplexer #(.select(4)) multiplexer_1 (
    .in0(1'b0), .in1(1'b0), .in2(1'b0), .in3(1'b0), .in4(1'b0), .in5(1'b0), .in6(1'b0), .in7(1'b0),
    .in8(1'b0), .in9(1'b1), .in10(1'b0), .in11(1'b1), .in12(1'b0), .in13(1'b0), .in14(1'b0), .in15(1'b0),
    .out(dmemAddr), .sel(icode));  // open: en
endmodule

// data
module dmemData (
  input  [3:0] icode,
  output dmemData
);

  Multiplexer #(.select(4)) multiplexer_1 (
    .in0(1'b0), .in1(1'b0), .in2(1'b0), .in3(1'b0), .in4(1'b0), .in5(1'b0), .in6(1'b0), .in7(1'b0),
    .in8(1'b1), .in9(1'b0), .in10(1'b0), .in11(1'b0), .in12(1'b0), .in13(1'b0), .in14(1'b0), .in15(1'b0),
    .out(dmemData), .sel(icode));  // open: en
endmodule

// dWri
module dmemWrite (
  input  [3:0] icode,
  output dmemWrite
);

  Multiplexer #(.select(4)) multiplexer_1 (
    .in0(1'b0), .in1(1'b0), .in2(1'b0), .in3(1'b0), .in4(1'b1), .in5(1'b0), .in6(1'b0), .in7(1'b0),
    .in8(1'b1), .in9(1'b0), .in10(1'b1), .in11(1'b0), .in12(1'b0), .in13(1'b0), .in14(1'b0), .in15(1'b0),
    .out(dmemWrite), .sel(icode));  // open: en
endmodule

// statVal
module newstatVal (
  input  [3:0] ifun,
  input  [3:0] icode,
  input  dmem,
  input  imem,
  output statWrite,
  output [1:0] statVal
);

  wire and_1_out, multiplexer_2_out, multiplexer_3_out, not_1_out, or_1_out, or_2_out, or_3_out, or_6_out;

  or or_1 (or_1_out, imem, and_1_out, or_6_out);
  and and_1 (and_1_out, not_1_out, 1'b1);
  Multiplexer #(.select(4)) multiplexer_1 (
    .in0(or_1_out), .in1(or_1_out), .in2(or_1_out), .in3(or_1_out), .in4(1'b1), .in5(1'b1), .in6(or_1_out),
    .in7(or_1_out), .in8(1'b1), .in9(1'b1), .in10(1'b1), .in11(1'b1), .in12(or_1_out), .in13(or_1_out),
    .in14(or_1_out), .in15(or_1_out), .out(statWrite), .sel(icode));  // open: en
  not not_1 (not_1_out, dmem);
  or or_2 (or_2_out, ifun[2], ifun[3]);
  or or_3 (or_3_out, ifun[1], ifun[0], ifun[2], ifun[3]);
  or or_4 (statVal[1], dmem, imem);
  or or_5 (statVal[0], or_6_out, dmem);
  or or_6 (or_6_out, multiplexer_2_out, multiplexer_3_out);
  Multiplexer #(.select(4)) multiplexer_2 (
    .in0(or_3_out), .in1(or_3_out), .in2(multiplexer_3_out), .in3(or_3_out), .in4(or_3_out), .in5(or_3_out),
    .in6(or_2_out), .in7(multiplexer_3_out), .in8(or_3_out), .in9(or_3_out), .in10(or_3_out),
    .in11(or_3_out), .in12(1'b1), .in13(1'b1), .in14(1'b1), .in15(1'b1), .out(multiplexer_2_out), .sel(icode));  // open: en
  Multiplexer #(.select(4)) multiplexer_3 (
    .in0(1'b0), .in1(1'b0), .in2(1'b0), .in3(1'b0), .in4(1'b0), .in5(1'b0), .in6(1'b0), .in7(1'b1),
    .in8(1'b1), .in9(1'b1), .in10(1'b1), .in11(1'b1), .in12(1'b1), .in13(1'b1), .in14(1'b1), .in15(1'b1),
    .out(multiplexer_3_out), .sel(ifun));  // open: en
endmodule
